# Fritzing sketch MRB (saved by Fritzing 0.9.9b)
breadboards: 1

parts:
  Part1 = Arduino Due (Rev2b)
  Power_plug1 = Power plug
  J1 = Basic Servo
  J2 = Basic Servo
  J3 = Basic Servo

nets:
  GND: Part1.GND, Power_plug1.GND, J1.gnd, J2.gnd, J3.gnd
  N1: Part1.D4_PWM/SS1, J3.pulse
  N2: Part1.D5_PWM, J2.pulse
  N3: Part1.D6_PWM, J1.pulse
  VCC: Power_plug1.VCC, J1.vcc, J2.vcc, J3.vcc
